# Fritzing sketch Handheld_Main (saved by Fritzing 0.9.3b)
circuit board: 4.93cm x 2.6169cm
breadboards: 1

parts:
  DN = Pushbutton [package="[THT]"]
  UP = Pushbutton [package="[THT]"]
  10k = Resistor [tolerance=±5% resistance=10k package=THT]
  10k_2 = Resistor [tolerance=±5% resistance=10k package=THT]
  10k_3 = Resistor [tolerance=±5% resistance=10k package=THT]
  ESP32_DEV_BOARD = ESP32S-HiLetgo [part_number=ESP32S-HiLetgo]
  G_+_SCREEN_CON = female pin header, 7 pins [form="♀ (female)"]
  BAT = female pin header, 2 pins [form="♀ (female)"]
  SW = Toggle Switch [package=THT]
  ENCODER_+_G = female pin header, 5 pins [form="♀ (female)"]

nets:
  N1: DN.Pin_1, DN.Pin_2, 10k_2.Pin_0, ESP32_DEV_BOARD.GPIO17
  N2: DN.Pin_3, DN.Pin_4, UP.Pin_3, UP.Pin_4, 10k.Pin_1, ESP32_DEV_BOARD.3.3, G_+_SCREEN_CON.pin6, ENCODER_+_G.pin2
  N3: UP.Pin_1, UP.Pin_2, 10k_3.Pin_0, ESP32_DEV_BOARD.GPIO16
  N4: 10k.Pin_0, ESP32_DEV_BOARD.GPIO26, ENCODER_+_G.pin3
  N5: 10k_2.Pin_1, 10k_3.Pin_1, ESP32_DEV_BOARD.GND, G_+_SCREEN_CON.pin7, BAT.pin2, ENCODER_+_G.pin1
  N6: ESP32_DEV_BOARD.GPIO27, ENCODER_+_G.pin4
  N7: ESP32_DEV_BOARD.GPIO14, ENCODER_+_G.pin5
  N8: ESP32_DEV_BOARD.VIN, SW.L2
  N9: ESP32_DEV_BOARD.GPIO15, G_+_SCREEN_CON.pin1
  N10: ESP32_DEV_BOARD.GPIO2, G_+_SCREEN_CON.pin3
  N11: ESP32_DEV_BOARD.GPIO4, G_+_SCREEN_CON.pin2
  N12: ESP32_DEV_BOARD.GPIO18, G_+_SCREEN_CON.pin5
  N13: ESP32_DEV_BOARD.GPIO23, G_+_SCREEN_CON.pin4
  N14: BAT.pin1, SW.L1, SW.COM

custom parts:
  ESP32S-HiLetgo: HiLetgo ESP-WROOM-32 ESP32 ESP-32S Development Board 2.4GHz Dual-Mode WiFi + Bluetooth Dual Cores Microcontroller The ESP32 integrated with Antenna switches, RF Balun, power amplifiers, low-noise amplifiers, filters, and management modules, and the entire solution occupies the least area of PCB. 2.4 GHz Wi-Fi plus Bluetooth dual-mode chip, with TSMC Ultra-low power consumption 40nm technology,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
